// Digital circuit 4 bit compare.dig as structural Verilog
module _4_bit_compare (
  input  [3:0] A,
  input  [3:0] B,
  output eq,
  output lt,
  output gt
);

  wire _1_bit_compare_1_p5, _1_bit_compare_1_p6, _1_bit_compare_2_p5, _1_bit_compare_2_p6,
       _1_bit_compare_3_p5, _1_bit_compare_3_p6, _1_bit_compare_4_p5, _1_bit_compare_4_p6, eq__1, eq__2,
       eq__3;

  // _1_bit_compare _1_bit_compare_1: pin names not known; wires that end beside it: 1'b1, A[3], B[3], eq__3, _1_bit_compare_1_p5, _1_bit_compare_1_p6
  // _1_bit_compare _1_bit_compare_2: pin names not known; wires that end beside it: eq__3, A[2], B[2], eq__2, _1_bit_compare_2_p5, _1_bit_compare_2_p6
  // _1_bit_compare _1_bit_compare_3: pin names not known; wires that end beside it: eq__2, A[1], B[1], eq__1, _1_bit_compare_3_p5, _1_bit_compare_3_p6
  // _1_bit_compare _1_bit_compare_4: pin names not known; wires that end beside it: eq__1, A[0], B[0], eq, _1_bit_compare_4_p5, _1_bit_compare_4_p6
  xor xor_1 (lt, _1_bit_compare_1_p5, _1_bit_compare_2_p6, _1_bit_compare_3_p6, _1_bit_compare_4_p6);
  xor xor_2 (gt, _1_bit_compare_1_p6, _1_bit_compare_2_p5, _1_bit_compare_3_p5, _1_bit_compare_4_p5);
endmodule
