// Digital circuit ALU.dig as structural Verilog
module ALU (
  input  [2:0] Opcode,
  input  [7:0] A,
  input  [7:0] B,
  output [7:0] S
);

  wire full_adder_8_bits_1_ov, full_subtraction_8_bits_1_ov, multiplication_4_bits_1_ov,
       multiplication_4_bits_1_ov_a, multiplication_4_bits_1_ov_b;
  wire [2:0] Comp_S;
  wire [7:0] Multi_S, Shift_S, Sub_S, Sum_S;

  Multiplexer #(.Bits(8), .Selector_Bits(3)) multiplexer_1 (
    .sel(Opcode), .in_0(Sum_S), .in_1(Sub_S), .in_2({{5{1'b0}}, Comp_S}), .in_3(Shift_S), .in_4(Multi_S),
    .in_5({8{1'b0}}), .in_6({8{1'b0}}), .in_7({8{1'b0}}), .out(S));
  LED led_1 (.in(full_adder_8_bits_1_ov));
  Full_Adder_8_bits full_adder_8_bits_1 (.A(A), .B(B), .Cin(1'b0), .S(Sum_S), .Ov(full_adder_8_bits_1_ov));
  Bit_shift_left bit_shift_left_1 (.A(A), .Out(Shift_S));
  LED led_2 (.in(full_subtraction_8_bits_1_ov));
  Full_Subtraction_8_bits full_subtraction_8_bits_1 (.A(A), .B(B), .S(Sub_S), .Ov(full_subtraction_8_bits_1_ov));
  Full_compare_8_bits full_compare_8_bits_1 (.A(B), .B(B), .eq(Comp_S[0]), .lt(Comp_S[1]), .gt(Comp_S[2]));
  LED led_3 (.in(multiplication_4_bits_1_ov_a));
  LED led_4 (.in(multiplication_4_bits_1_ov_b));
  LED led_5 (.in(multiplication_4_bits_1_ov));
  Multiplication_4_bits multiplication_4_bits_1 (
    .A(B[3:0]), .B(A[3:0]), .S(Multi_S), .Ov(multiplication_4_bits_1_ov),
    .Ov_B(multiplication_4_bits_1_ov_b), .Ov_A(multiplication_4_bits_1_ov_a));
endmodule
