// Digital circuit Full Subtraction 8 bits.dig as structural Verilog
module Full_Subtraction_8_bits (
  input  [7:0] A,
  input  [7:0] B,
  output [7:0] S,
  output Ov
);

  wire [7:0] not_1_out;

  assign not_1_out = ~B;  // Not not_1, 8 bits wide
  Full_Adder_8_bits full_adder_8_bits_1 (.A(A), .B(not_1_out), .Cin(1'b1), .S(S), .Ov(Ov));
endmodule
