// Digital circuit Full adder 4 bits.dig as structural Verilog
module Full_adder_4_bits (
  input  [3:0] A,
  input  [3:0] B,
  input  Cin,
  output [3:0] S,
  output Ov
);

  wire full_adder_1_cout, full_adder_2_cout, full_adder_3_cout, full_adder_4_cout;

  full_adder full_adder_1 (.A(A[0]), .B(B[0]), .Cin(Cin), .Cout(full_adder_1_cout), .S(S[0]));
  full_adder full_adder_2 (.A(A[1]), .B(B[1]), .Cin(full_adder_1_cout), .Cout(full_adder_2_cout), .S(S[1]));
  full_adder full_adder_3 (.A(A[2]), .B(B[2]), .Cin(full_adder_2_cout), .Cout(full_adder_3_cout), .S(S[2]));
  full_adder full_adder_4 (.A(A[3]), .B(B[3]), .Cin(full_adder_3_cout), .Cout(full_adder_4_cout), .S(S[3]));
  xor xor_1 (Ov, full_adder_4_cout, full_adder_3_cout);
endmodule
