// Digital circuit Full compare 8 bits.dig as structural Verilog
module Full_compare_8_bits (
  input  [7:0] A,
  input  [7:0] B,
  output eq,
  output lt,
  output gt
);

  wire _1_bit_compare_1_p5, _1_bit_compare_1_p6, _1_bit_compare_2_p5, _1_bit_compare_2_p6,
       _1_bit_compare_3_p5, _1_bit_compare_3_p6, _1_bit_compare_4_p5, _1_bit_compare_4_p6,
       _1_bit_compare_5_p5, _1_bit_compare_5_p6, _1_bit_compare_6_p5, _1_bit_compare_6_p6,
       _1_bit_compare_7_p5, _1_bit_compare_7_p6, _1_bit_compare_8_p5, _1_bit_compare_8_p6, eq__1, eq__2,
       eq__3, eq__4, eq__5, eq__6, eq__7;

  // _1_bit_compare _1_bit_compare_1: pin names not known; wires that end beside it: 1'b1, A[7], B[7], eq__7, _1_bit_compare_1_p5, _1_bit_compare_1_p6
  // _1_bit_compare _1_bit_compare_2: pin names not known; wires that end beside it: eq__7, A[6], B[6], eq__6, _1_bit_compare_2_p5, _1_bit_compare_2_p6
  // _1_bit_compare _1_bit_compare_3: pin names not known; wires that end beside it: eq__6, A[5], B[5], eq__5, _1_bit_compare_3_p5, _1_bit_compare_3_p6
  // _1_bit_compare _1_bit_compare_4: pin names not known; wires that end beside it: eq__5, A[4], B[4], eq__4, _1_bit_compare_4_p5, _1_bit_compare_4_p6
  // _1_bit_compare _1_bit_compare_5: pin names not known; wires that end beside it: eq__4, A[3], B[3], eq__3, _1_bit_compare_5_p5, _1_bit_compare_5_p6
  // _1_bit_compare _1_bit_compare_6: pin names not known; wires that end beside it: eq__3, A[2], B[2], eq__2, _1_bit_compare_6_p5, _1_bit_compare_6_p6
  // _1_bit_compare _1_bit_compare_7: pin names not known; wires that end beside it: eq__2, A[1], B[1], eq__1, _1_bit_compare_7_p5, _1_bit_compare_7_p6
  // _1_bit_compare _1_bit_compare_8: pin names not known; wires that end beside it: eq__1, A[0], B[0], eq, _1_bit_compare_8_p5, _1_bit_compare_8_p6
  xor xor_1 (lt, _1_bit_compare_1_p5, _1_bit_compare_2_p6, _1_bit_compare_3_p6, _1_bit_compare_4_p6, _1_bit_compare_5_p6, _1_bit_compare_6_p6, _1_bit_compare_7_p6, _1_bit_compare_8_p6);
  xor xor_2 (gt, _1_bit_compare_1_p6, _1_bit_compare_2_p5, _1_bit_compare_3_p5, _1_bit_compare_4_p5, _1_bit_compare_5_p5, _1_bit_compare_6_p5, _1_bit_compare_7_p5, _1_bit_compare_8_p5);
endmodule
