// Digital circuit Multiplication 4 bits.dig as structural Verilog
module Multiplication_4_bits (
  input  [3:0] A,
  input  [3:0] B,
  output [7:0] S,
  output Ov,
  output Ov_B,
  output Ov_A
);

  wire _4_bit_compare_1_eq, _4_bit_compare_1_lt, A0, A1, A2, A3, B0, B1, B2, B3, Both_Neg, Change,
       full_adder_4_bits_1_ov, full_adder_4_bits_2_ov, full_adder_4_bits_5_ov, full_adder_4_bits_6_ov,
       full_adder_8_bits_2_ov, full_adder_8_bits_3_ov, Neg, Not_Both_Neg, Not_Change;
  wire [3:0] A_t, and_2_out, and_10_out, B_t, Change_A, Change_B, Normal_A, Normal_B, not_1_out, not_3_out,
       Not_A, Not_B, Not_Change_A, Not_Change_B;
  wire [7:0] and_7_out, and_20_out, and_21_out, bit_shift_left_1_out, bit_shift_left_4_out,
       bit_shift_left_5_out, C0, C1, C2, C3, full_adder_8_bits_2_s, full_adder_8_bits_3_s;

  and and_1 (Both_Neg, A[3], B[3]);
  LED led_1 (.in(full_adder_4_bits_1_ov));
  Full_adder_4_bits full_adder_4_bits_1 (
    .A(not_1_out), .B(4'b0000), .Cin(1'b1), .S(Not_A), .Ov(full_adder_4_bits_1_ov));
  assign not_1_out = ~and_2_out;  // Not not_1, 4 bits wide
  and and_2 (and_2_out[0], A[0], Both_Neg);
  not not_2 (Not_Both_Neg, Both_Neg);
  and and_3 (and_2_out[1], A[1], Both_Neg);
  and and_4 (and_2_out[2], A[2], Both_Neg);
  and and_5 (and_2_out[3], A[3], Both_Neg);
  and and_6 (C0[0], A0, B0);
  and and_7 (and_7_out[7], B2, Neg);
  and and_8 (C0[1], A1, B0);
  and and_9 (and_7_out[3], A3, B2);
  LED led_2 (.in(full_adder_4_bits_2_ov));
  Full_adder_4_bits full_adder_4_bits_2 (
    .A(not_3_out), .B(4'b0000), .Cin(1'b1), .S(Not_B), .Ov(full_adder_4_bits_2_ov));
  assign not_3_out = ~and_10_out;  // Not not_3, 4 bits wide
  and and_10 (and_10_out[0], B[0], Both_Neg);
  and and_11 (C0[2], A2, B0);
  and and_12 (and_7_out[2], A2, B2);
  and and_13 (and_10_out[1], B[1], Both_Neg);
  and and_14 (C0[3], A3, B0);
  and and_15 (and_10_out[2], B[2], Both_Neg);
  and and_16 (and_7_out[1], A1, B2);
  and and_17 (C0[7], B0, Neg);
  and and_18 (and_7_out[0], A0, B2);
  Bit_shift_left bit_shift_left_1 (.A({{4{and_7_out[7]}}, and_7_out[3:0]}), .Out(bit_shift_left_1_out));
  Bit_shift_left bit_shift_left_2 (.A(bit_shift_left_1_out), .Out(C2));
  and and_19 (and_10_out[3], B[3], Both_Neg);
  Bit_shift_left bit_shift_left_3 (.A({{4{and_20_out[7]}}, and_20_out[3:0]}), .Out(C1));
  and and_20 (and_20_out[0], A0, B1);
  and and_21 (and_21_out[7], B3, Neg);
  and and_22 (Normal_B[0], B[0], Not_Both_Neg);
  and and_23 (and_20_out[1], A1, B1);
  and and_24 (and_21_out[3], A3, B3);
  and and_25 (Normal_B[1], B[1], Not_Both_Neg);
  and and_26 (and_20_out[2], A2, B1);
  and and_27 (Normal_B[2], B[2], Not_Both_Neg);
  and and_28 (and_21_out[2], A2, B3);
  Full_adder_4_bits full_adder_4_bits_3 (.A(Normal_A), .B(Not_A), .Cin(1'b0), .S(A_t), .Ov(Ov_A));
  and and_29 (and_20_out[3], A3, B1);
  and and_30 (Normal_B[3], B[3], Not_Both_Neg);
  and and_31 (and_21_out[1], A1, B3);
  and and_32 (and_20_out[7], B1, Neg);
  Bit_shift_left bit_shift_left_4 (.A({{4{and_21_out[7]}}, and_21_out[3:0]}), .Out(bit_shift_left_4_out));
  Bit_shift_left bit_shift_left_5 (.A(bit_shift_left_4_out), .Out(bit_shift_left_5_out));
  Bit_shift_left bit_shift_left_6 (.A(bit_shift_left_5_out), .Out(C3));
  and and_33 (and_21_out[0], A0, B3);
  xor xor_1 (Neg, A[3], B[3]);
  Full_adder_4_bits full_adder_4_bits_4 (.A(Normal_B), .B(Not_B), .Cin(1'b0), .S(B_t), .Ov(Ov_B));
  Full_Adder_8_bits full_adder_8_bits_1 (
    .A(full_adder_8_bits_2_s), .B(C3), .Cin(full_adder_8_bits_2_ov), .S(S), .Ov(Ov));
  Full_Adder_8_bits full_adder_8_bits_2 (
    .A(full_adder_8_bits_3_s), .B(C2), .Cin(full_adder_8_bits_3_ov), .S(full_adder_8_bits_2_s),
    .Ov(full_adder_8_bits_2_ov));
  Full_Adder_8_bits full_adder_8_bits_3 (
    .A({{4{C0[7]}}, C0[3:0]}), .B(C1), .Cin(1'b0), .S(full_adder_8_bits_3_s), .Ov(full_adder_8_bits_3_ov));
  and and_34 (Normal_A[0], A[0], Not_Both_Neg);
  and and_35 (Normal_A[1], A[1], Not_Both_Neg);
  and and_36 (Normal_A[2], A[2], Not_Both_Neg);
  _4_bit_compare _4_bit_compare_1 (.A(A_t), .B(B_t), .eq(_4_bit_compare_1_eq), .lt(_4_bit_compare_1_lt), .gt(Change));
  and and_37 (Normal_A[3], A[3], Not_Both_Neg);
  or or_1 (Not_Change, _4_bit_compare_1_eq, _4_bit_compare_1_lt);
  and and_38 (Change_B[0], A_t[0], Change);
  and and_39 (Change_B[1], A_t[1], Change);
  and and_40 (Change_B[2], A_t[2], Change);
  Full_adder_4_bits full_adder_4_bits_5 (
    .A(Not_Change_A), .B(Change_A), .Cin(1'b0), .S({A3, A2, A1, A0}), .Ov(full_adder_4_bits_5_ov));
  Full_adder_4_bits full_adder_4_bits_6 (
    .A(Not_Change_B), .B(Change_B), .Cin(1'b0), .S({B3, B2, B1, B0}), .Ov(full_adder_4_bits_6_ov));
  and and_41 (Change_B[3], A_t[3], Change);
  LED led_3 (.in(full_adder_4_bits_5_ov));
  LED led_4 (.in(full_adder_4_bits_6_ov));
  and and_42 (Change_A[0], B_t[0], Change);
  and and_43 (Change_A[1], B_t[1], Change);
  and and_44 (Change_A[2], B_t[2], Change);
  and and_45 (Change_A[3], B_t[3], Change);
  and and_46 (Not_Change_A[0], A_t[0], Not_Change);
  and and_47 (Not_Change_A[1], A_t[1], Not_Change);
  and and_48 (Not_Change_A[2], A_t[2], Not_Change);
  and and_49 (Not_Change_A[3], A_t[3], Not_Change);
  and and_50 (Not_Change_B[0], B_t[0], Not_Change);
  and and_51 (Not_Change_B[1], B_t[1], Not_Change);
  and and_52 (Not_Change_B[2], B_t[2], Not_Change);
  and and_53 (Not_Change_B[3], B_t[3], Not_Change);

  // Other names for the same wires on the sheet: C0[6:4] = {3{C0[7]}}; A0_Raw = A[0]; A1_Raw = A[1]; A2_Raw = A[2];
  //   A3_Raw = A[3]; Preview_A0 = A_t[0]; Preview_A1 = A_t[1]; Preview_A2 = A_t[2]; Preview_A3 = A_t[3];
  //   B0_Raw = B[0]; B1_Raw = B[1]; B2_Raw = B[2]; B3_Raw = B[3]; Preview_B0 = B_t[0]; Preview_B1 = B_t[1];
  //   Preview_B2 = B_t[2]; Preview_B3 = B_t[3]
endmodule
