// Digital circuit display.dig as structural Verilog
module display (
  input  [7:0] A,
  input  [7:0] B,
  input  [2:0] Opcode,
  output [7:0] S
);

  ALU alu_1 (.Opcode(Opcode), .A(A), .B(B), .S(S));
  Seven_Seg_Hex seven_seg_hex_1 (.d(S[3:0]), .dp(S[7]));
endmodule
