// Digital circuit full-adder.dig as structural Verilog
module full_adder (
  input  A,
  input  B,
  input  Cin,
  output Cout,
  output S
);

  wire half_adder_1_carry_out, half_adder_1_sum, half_adder_2_carry_out;

  half_adder half_adder_1 (.A(A), .B(B), .Sum(half_adder_1_sum), .Carry_out(half_adder_1_carry_out));
  half_adder half_adder_2 (.A(half_adder_1_sum), .B(Cin), .Sum(S), .Carry_out(half_adder_2_carry_out));
  or or_1 (Cout, half_adder_1_carry_out, half_adder_2_carry_out);
endmodule
