// Digital circuit half-adder.dig as structural Verilog
module half_adder (
  input  A,
  input  B,
  output Sum,
  output Carry_out
);

  xor xor_1 (Sum, A, B);
  and and_1 (Carry_out, A, B);
endmodule
